# Fritzing sketch a1_5Vpower (saved by Fritzing 0.6.2b)
breadboards: 1

parts:
  Arduino1 = Arduino
  R1 = Resistor [tolerance=±5% resistance=150 package=THT]
  LED1 = Red LED - 5mm [package="5 mm [THT]"]

nets:
  N1: Arduino1.+5V, R1.Pin_1
  N2: Arduino1.GND, LED1.cathode
  N3: R1.Pin_0, LED1.anode
