# Fritzing sketch a2_pushbutton (saved by Fritzing 0.6.2b)
breadboards: 1

parts:
  R2 = Resistor [tolerance=±5% resistance=10k package=THT]
  S1 = Pushbutton [package="[THT]"]
  LED1 = Red LED - 5mm [package="5 mm [THT]"]
  Arduino2 = Arduino

nets:
  N1: R2.Pin_0, LED1.cathode, Arduino2.GND
  N2: R2.Pin_1, S1.Pin_3, S1.Pin_4, Arduino2.D2
  N3: S1.Pin_1, S1.Pin_2, Arduino2.+5V
  N4: LED1.anode, Arduino2.D13
