# Fritzing sketch potentiometer-led-schematic (saved by Fritzing 0.4.3b)
breadboards: 1

parts:
  Arduino1 = Arduino
  LED1 = Red LED - 5mm
  R1 = Rotary Potentiometer (Large) [package=THT]
  R2 = Resistor [resistance=1k package=THT]

nets:
  N1: Arduino1.GND, R1.wiper, R2.Pin_0
  N2: Arduino1.D9, LED1.anode
  N3: Arduino1.+5V, R1.leg2
  N4: Arduino1.A0, R1.leg1
  N5: LED1.cathode, R2.Pin_1
