# Fritzing sketch photoresistor-schematic (saved by Fritzing 0.9.3b)
breadboards: 1

parts:
  R2 = Resistor [tolerance=±5% resistance=10k package=THT]
  R3 = Photocell (LDR) [package=THT]
  R4 = Resistor [tolerance=±5% resistance=220 package=THT]
  LED1 = LED - 5mm [color="Red (633nm)" package="5 mm [THT]"]
  Arduino2 = Arduino Uno (Rev3)

nets:
  N1: R2.Pin_0, LED1.cathode, Arduino2.GND
  N2: R2.Pin_1, R3.pin_0, Arduino2.A2
  N3: R4.Pin_0, LED1.anode
