# Fritzing sketch temp-sensor-3-wire-schematic (saved by Fritzing 0.9.3b)
breadboards: 1

parts:
  R1 = Resistor [tolerance=±5% resistance=4.7k package=THT]
  Actually_a_3-wire_temp_sensor = NPN-Transistor [package="TO92 [THT]"]
  Arduino1 = Arduino Uno (Rev3)

nets:
  N1: R1.Pin_0, Actually_a_3-wire_temp_sensor.B
  N2: R1.Pin_1, Actually_a_3-wire_temp_sensor.C
  N3: Actually_a_3-wire_temp_sensor.E, Arduino1.GND
