# Fritzing sketch temp36-schematic (saved by Fritzing 0.9.3b)
breadboards: 1

parts:
  Q1 = PNP-Transistor [package="TO92 [THT]"]
  Arduino3 = Arduino Uno (Rev3)

nets:
  N1: Q1.B, Arduino3.A0
  N2: Q1.C, Arduino3.GND

notes:
  This is actually a TEMP36 temperature sensor
  http://dlnmh9ip6v2uc.cloudfront.net/datasheets/Sensors/Temp/TMP35_36_37.pdf
