# Fritzing sketch DIY Arduino (saved by Fritzing 0.9.3b)
breadboards: 2

parts:
  U1 = atmega328 [package=dip]  # not connected
  C1 = Electrolytic Capacitor [capacitance=10µF package="100 mil [THT, electrolytic]"]  # not connected
  C3 = Ceramic Capacitor [capacitance=22µF package="100 mil [THT, multilayer]"]  # not connected
  C4 = Electrolytic Capacitor [capacitance=10µF package="100 mil [THT, electrolytic]"]  # not connected
  R1 = Resistor [tolerance=±5% resistance=220 package=THT]  # not connected
  R2 = Resistor [tolerance=±5% resistance=220 package=THT]  # not connected
  R3 = Resistor [tolerance=±5% resistance=10k package=THT]  # not connected
  U2 = Voltage Regulator - 5V [package="TO220 [THT]"]  # not connected
  S1 = Pushbutton [package="[THT]"]  # not connected
  XTAL1 = Crystal [frequency="16 Mhz" package=THT]  # not connected
  LED1 = LED - 5mm [color="Red (633nm)" package="5 mm [THT]"]  # not connected
  LED2 = LED - 5mm [color="Green (565nm)" package="5 mm [THT]"]  # not connected
  C5 = Ceramic Capacitor [capacitance=22µF package="100 mil [THT, multilayer]"]  # not connected
  VCC1 = Battery block 9V  # not connected
  U3 = atmega328 [package=dip]
  C6 = Electrolytic Capacitor [capacitance=10µF package="100 mil [THT, electrolytic]"]
  C7 = Electrolytic Capacitor [capacitance=10µF package="100 mil [THT, electrolytic]"]
  C8 = Ceramic Capacitor [capacitance=22µF package="100 mil [THT, multilayer]"]
  C9 = Ceramic Capacitor [capacitance=22µF package="100 mil [THT, multilayer]"]
  R4 = Resistor [tolerance=±5% resistance=220 package=THT]
  R5 = Resistor [tolerance=±5% resistance=220 package=THT]
  R6 = Resistor [tolerance=±5% resistance=10k package=THT]
  U4 = Voltage Regulator - 5V [package="TO220 [THT]"]
  S2 = Pushbutton [package="[THT]"]
  XTAL2 = Crystal [frequency="16 Mhz" package=THT]
  LED3 = LED - 5mm [color="Green (565nm)" package="5 mm [THT]"]
  LED4 = LED - 5mm [color="Red (633nm)" package="5 mm [THT]"]
  VCC2 = Battery block 9V

nets:
  N1: U3.RESET, R6.Pin_0, S2.Pin_1, S2.Pin_2
  N2: U3.VCC, U3.AVCC, U3.AREF, C6.+, C8.1, C9.1, R6.Pin_1, U4.output_voltage, LED4.anode
  GND: U3.GND, C6.-, C7.-, R5.Pin_0, U4.GND, S2.Pin_3, S2.Pin_4, LED3.cathode, VCC2.-
  N3: U3.XLAT1, C9.0, XTAL2.pin_0
  N4: U3.XLAT2, C8.0, XTAL2.pin_1
  N5: U3.D13, R4.Pin_0
  N6: C7.+, U4.input_voltage, VCC2.+
  N7: R4.Pin_1, LED3.anode
  N8: R5.Pin_1, LED4.cathode
