# Fritzing sketch sensors-light-temp-schematic (saved by Fritzing 0.7.4b)
breadboards: 1

parts:
  T1 = TMP36 Temperature Sensor [package="TO92 [THT]"]
  R1 = Resistor [tolerance=±5% resistance=1k package=THT]
  BeagleBone1 = BeagleBone
  R3 = Resistor [tolerance=±5% resistance=1.2k package=THT]
  R4 = Photocell (LDR) [package=THT]
  R5 = Resistor [tolerance=±5% resistance=10k package=THT]

nets:
  N1: T1.Vout, R1.Pin_1
  N2: T1.GND, BeagleBone1.no_name_yet#connectorp9-4, R3.Pin_0
  N3: R1.Pin_0, BeagleBone1.no_name_yet#connectorp9-38, R3.Pin_1
  N4: BeagleBone1.no_name_yet#connectorp9-32, R4.pin_1
  N5: BeagleBone1.no_name_yet#connectorp9-34, R5.Pin_0
  N6: BeagleBone1.no_name_yet#connectorp9-39, R4.pin_0, R5.Pin_1
