# Fritzing sketch button (saved by Fritzing 0.9.3b)
breadboards: 1

parts:
  Raspberry_Pi_1 = Raspberry Pi 3 [part_number=RPI-3-V1.2]
  pull-up_circuit = Pushbutton [package="[THT]"]
  pull-down_circuit = Pushbutton [package="[THT]"]

nets:
  N1: Raspberry_Pi_1.3v3, pull-down_circuit.Pin_3, pull-down_circuit.Pin_4
  N2: Raspberry_Pi_1.GPIO2, pull-down_circuit.Pin_1, pull-down_circuit.Pin_2
  N3: Raspberry_Pi_1.GND, pull-up_circuit.Pin_3, pull-up_circuit.Pin_4
  N4: Raspberry_Pi_1.GPIO21, pull-up_circuit.Pin_1, pull-up_circuit.Pin_2
